# Fritzing sketch Arduino_MenuLcd (saved by Fritzing 0.9.3b)
breadboards: 1

parts:
  LCD1 = LCD screen
  Componente2 = Arduino Uno (Rev3) - ICSP
  S1 = Pushbutton [package="[THT]"]
  S2 = Pushbutton [package="[THT]"]
  S3 = Pushbutton [package="[THT]"]
  R1 = TRIMPOT [package=3362u-2]
  J1 = Piezo Speaker

nets:
  VSS: LCD1.VSS, LCD1.R/W, LCD1.LED-, Componente2.GND, S1.Pin_1, S1.Pin_2, S2.Pin_1, S2.Pin_2, S3.Pin_1, S3.Pin_2, J1.pin1
  VDD: LCD1.VDD, LCD1.LED+, Componente2.5V
  N1: LCD1.V0, R1.WIPER
  N2: LCD1.RS, Componente2.D12/MISO
  N3: LCD1.E, Componente2.D11_PWM/MOSI
  N4: LCD1.DB4, Componente2.D5_PWM
  N5: LCD1.DB5, Componente2.D4
  N6: LCD1.DB6, Componente2.D3_PWM
  N7: LCD1.DB7, Componente2.D2
  N8: Componente2.D8, S1.Pin_3, S1.Pin_4
  N9: Componente2.D9_PWM, J1.pin2
  N10: Componente2.D6_PWM, S3.Pin_3, S3.Pin_4
  N11: Componente2.D7, S2.Pin_3, S2.Pin_4
